# Fritzing sketch elepaja (saved by Fritzing 0.9.9b)
stripboards: 1

parts:
  R1 = Resistor [tolerance=±5% resistance=4.7k power=0.25 package=THT]
  R3 = Resistor [tolerance=±5% resistance=8k power=0.25 package=THT]
  C1 = Ceramic Capacitor [capacitance=100nF package="100 mil [THT, multilayer]"]
  R4 = Resistor [tolerance=±5% resistance=12k power=0.25 package=THT]
  U1 = LM 358 Dual Op-Amp [package="DIP8 [THT]"]
  R5 = Resistor [tolerance=±5% resistance=12k power=0.25 package=THT]
  R6 = Resistor [tolerance=±5% resistance=4.7k power=0.25 package=THT]
  C2 = Ceramic Capacitor [capacitance=100nF package="100 mil [THT, multilayer]"]
  R7 = Resistor [tolerance=±5% resistance=8k power=0.25 package=THT]
  U2 = LM 358 Dual Op-Amp [package="DIP8 [THT]"]
  C3 = Ceramic Capacitor [capacitance=100nF package="100 mil [THT, multilayer]"]
  R8 = Resistor [tolerance=±5% resistance=8k power=0.25 package=THT]
  R9 = Resistor [tolerance=±5% resistance=12k power=0.25 package=THT]
  R10 = Resistor [tolerance=±5% resistance=4.7k power=0.25 package=THT]
  R11 = Resistor [tolerance=±5% resistance=12k power=0.25 package=THT]
  R12 = Resistor [tolerance=±5% resistance=4.7k power=0.25 package=THT]
  C4 = Ceramic Capacitor [capacitance=100nF package="100 mil [THT, multilayer]"]
  R13 = Resistor [tolerance=±5% resistance=8k power=0.25 package=THT]

nets:
  5V/GND: R1.Pin_0, C1.1, U1.connector3, U1.connector7, R6.Pin_0, C2.0, U2.connector3, U2.connector7, C3.0, R10.Pin_1, R12.Pin_1, C4.1
  N1: R1.Pin_1, R4.Pin_1, U1.connector1
  N2: R3.Pin_1, C1.0, U1.connector2
  N3: R4.Pin_0, U1.connector0
  N4: U1.connector4, C2.1, R7.Pin_1
  N5: U1.connector5, R5.Pin_1, R6.Pin_1
  N6: U1.connector6, R5.Pin_0
  N7: U2.connector0, R9.Pin_1
  N8: U2.connector1, R9.Pin_0, R10.Pin_0
  N9: U2.connector2, C3.1, R8.Pin_0
  N10: U2.connector4, C4.0, R13.Pin_0
  N11: U2.connector5, R11.Pin_0, R12.Pin_0
  N12: U2.connector6, R11.Pin_1
